# Fritzing sketch chess (saved by Fritzing 0.9.3b)
breadboards: 1

parts:
  IC2 = MCP23017 I2C I/O Expander
  Part2 = HT16K33 Breakout 16x8 LED Matrix Driver [part_number=1427]
  catodes = male pin header, 8 pins [form="♂ (male)"]  # not connected
  anodes = male pin header, 8 pins [form="♂ (male)"]  # not connected
  J7 = male pin header, 8 pins [form="♂ (male)"]  # not connected
  J8 = male pin header, 8 pins [form="♂ (male)"]  # not connected
  J11 = female pin header, 2 pins [form="♀ (female)"]  # not connected
  J46 = female pin header, 5 pins [form="♀ (female)"]  # not connected
  J47 = female pin header, 3 pins [form="♀ (female)"]  # not connected
  J48 = female pin header, 4 pins [form="♀ (female)"]  # not connected
  5V = female pin header, 1 pin [form="♀ (female)"]
  gnd = female pin header, 1 pin [form="♀ (female)"]
  GND = female pin header, 1 pin [form="♀ (female)"]
  GND_2 = female pin header, 1 pin [form="♀ (female)"]
  GND_3 = female pin header, 1 pin [form="♀ (female)"]
  5V_2 = female pin header, 1 pin [form="♀ (female)"]
  5V_3 = female pin header, 1 pin [form="♀ (female)"]
  5V_4 = female pin header, 1 pin [form="♀ (female)"]
  sda1 = female pin header, 1 pin [form="♀ (female)"]
  scl1 = female pin header, 1 pin [form="♀ (female)"]
  catodes1 = male pin header, 8 pins [form="♂ (male)"]  # not connected
  J49 = female pin header, 2 pins [form="♀ (female)"]  # not connected
  slc = female pin header, 1 pin [form="♀ (female)"]
  sda = female pin header, 1 pin [form="♀ (female)"]
  VCC2 = Battery  # not connected

nets:
  N1: IC2.VDD, 5V_2.pin1
  N2: IC2.VSS, GND.pin1
  N3: IC2.SCL, slc.pin1
  N4: IC2.SDA, sda.pin1
  N5: IC2.A0, 5V_4.pin1
  N6: IC2.A1, GND_3.pin1
  N7: IC2.A2, GND_2.pin1
  N8: IC2.RESET, 5V_3.pin1
  N9: Part2.SCL, scl1.pin1
  N10: Part2.SDA, sda1.pin1
  N11: Part2.VDD, 5V.pin1
  N12: Part2.GND, gnd.pin1

notes:
  cut

custom parts:
  MCP23017 I2C I/O Expander: The MCP23017 uses two i2c pins (these can be shared with other i2c devices), and in exchange gives you 16 general purpose pins. You can set each of 16 pins to be input, output, input with a pullup or open drain. There's even the ability to get an interrupt via an external pin when any of the inputs change so you don't have to keep polling the chip.
  HT16K33 Breakout 16x8 LED Matrix Driver: This is the magic sauce in our 7-segment and matrix backpacks, now available in breadboard-friendly breakout board format. The HT16K33 is a neat little chip that has the ability to drive a multiplexed 16x8 matrix (that's 128 individual LEDs). The communication protocol is I2C so it uses only 2 pins, and you can have up to 8 selectable I2C addresses so thats a total of 8 matrices, each one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
